// Logisim project Braille_Nicolle.circ TESTE2.circ as structural Verilog
module main (
  input  b6,
  input  b5,
  input  b4,
  input  b3,
  input  b1,
  input  b2
);

  wire multiplexer_1_out, multiplexer_2_out, multiplexer_3_out, multiplexer_4_out, multiplexer_5_out,
       multiplexer_6_out;

  Multiplexer #(.select(2), .enable("false")) multiplexer_1 (
    .in0(b3), .in1(b4), .in2(b5), .in3(b6), .out(multiplexer_1_out), .sel({b2, b1}));
  LED A (.in(multiplexer_1_out));
  LED B (.in(multiplexer_2_out));
  LED C (.in(multiplexer_3_out));
  LED D (.in(multiplexer_4_out));
  LED E (.in(multiplexer_5_out));
  LED F (.in(multiplexer_6_out));
  Multiplexer #(.select(2), .enable("false")) multiplexer_2 (
    .in0(b3), .in1(b4), .in2(b5), .in3(b6), .out(multiplexer_2_out), .sel({b2, b1}));
  Multiplexer #(.select(2), .enable("false")) multiplexer_3 (
    .in0(b3), .in1(b4), .in2(b5), .in3(b6), .out(multiplexer_3_out), .sel({b2, b1}));
  Multiplexer #(.select(2), .enable("false")) multiplexer_4 (
    .in0(b3), .in1(b4), .in2(b5), .in3(b6), .out(multiplexer_4_out), .sel({b2, b1}));
  Multiplexer #(.select(2), .enable("false")) multiplexer_5 (
    .in0(b3), .in1(b4), .in2(b5), .in3(b6), .out(multiplexer_5_out), .sel({b2, b1}));
  Multiplexer #(.select(2), .enable("false")) multiplexer_6 (
    .in0(b3), .in1(b4), .in2(b5), .in3(b6), .out(multiplexer_6_out), .sel({b2, b1}));
endmodule

module circuito_A00 (
  input  b6,
  input  b1,
  input  b2,
  input  b5,
  input  b4,
  input  b3,
  input  b6_2,
  input  b5_2,
  input  b4_2,
  input  b6_3,
  input  b3_2,
  input  b5_3,
  input  b1_2,
  input  b2_2,
  input  b1_3,
  input  b2_3,
  input  b4_3,
  input  b3_3,
  output A00,
  output A01,
  output A11
);

  wire and_1_out, and_2_out, and_3_out, and_4_out, and_5_out, and_6_out, and_7_out, and_9_out, and_10_out,
       and_12_out, and_13_out, and_14_out, and_15_out, and_16_out, and_17_out, or_1_out, or_2_out, or_3_out,
       or_4_out, or_5_out, or_6_out, or_7_out, or_8_out, or_9_out, or_10_out, or_11_out, or_12_out, or_13_out;

  and and_1 (and_1_out, ~b1_3, ~b2_3);  // AND_Gate
  and and_2 (and_2_out, ~b1_3, b2_3);  // AND_Gate
  and and_3 (and_3_out, b1_3, b2_3);
  and and_4 (and_4_out, ~b1, ~b2);  // AND_Gate
  and and_5 (and_5_out, ~b1, b2);  // AND_Gate
  and and_6 (and_6_out, b1, b2);
  or or_1 (or_1_out, and_1_out, and_2_out);
  or or_2 (or_2_out, and_4_out, and_5_out);
  or or_3 (or_3_out, or_2_out, and_6_out);
  or or_4 (or_4_out, or_1_out, and_3_out);
  or or_5 (or_5_out, b3, b4);
  or or_6 (or_6_out, or_5_out, ~b5);  // OR_Gate
  and and_7 (and_7_out, or_6_out, b6);
  or or_7 (or_7_out, b4_3, b5_3);
  and and_8 (A00, and_7_out, or_3_out);
  and and_9 (and_9_out, or_7_out, b3_3);
  and and_10 (and_10_out, and_9_out, b6_3);
  and and_11 (A01, and_10_out, or_4_out);
  and and_12 (and_12_out, ~b1_2, ~b2_2);  // AND_Gate
  and and_13 (and_13_out, ~b1_2, b2_2);  // AND_Gate
  and and_14 (and_14_out, b1_2, b2_2);
  or or_8 (or_8_out, and_12_out, and_13_out);
  or or_9 (or_9_out, or_8_out, and_14_out);
  or or_10 (or_10_out, b3_2, ~b3_2);  // OR_Gate
  or or_11 (or_11_out, or_10_out, ~b5_2);  // OR_Gate
  or or_12 (or_12_out, or_11_out, b6_2);
  or or_13 (or_13_out, or_12_out, b4_2);
  and and_15 (and_15_out, or_13_out, ~b4_2);  // AND_Gate
  and and_16 (and_16_out, and_15_out, b5_2);
  and and_17 (and_17_out, and_16_out, b6_2);
  and and_18 (A11, and_17_out, or_9_out);
endmodule

module SubCircuito_B (
  input  b6,
  input  b6_2,
  input  b5,
  input  b5_2,
  input  b1,
  input  b2,
  input  b1_2,
  input  b2_2,
  input  b4,
  input  b4_2,
  input  b3,
  input  b3_2,
  output B00,
  output B00_2
);

  wire and_1_out, and_2_out, and_3_out, and_4_out, and_6_out, and_7_out, and_8_out, and_9_out, or_1_out,
       or_2_out, or_3_out, or_4_out, or_5_out, or_6_out, or_7_out;

  and and_1 (and_1_out, ~b1, ~b2);  // AND_Gate
  and and_2 (and_2_out, ~b1, b2);  // AND_Gate
  and and_3 (and_3_out, b1, b2);
  or or_1 (or_1_out, and_1_out, and_2_out);
  or or_2 (or_2_out, or_1_out, and_3_out);
  or or_3 (or_3_out, b4, b3);
  or or_4 (or_4_out, or_3_out, ~b4);  // OR_Gate
  or or_5 (or_5_out, or_4_out, ~b6);  // OR_Gate
  and and_4 (and_4_out, or_5_out, b5);
  and and_5 (B00, and_4_out, or_2_out);
  and and_6 (and_6_out, ~b1_2, ~b2_2);  // AND_Gate
  or or_6 (or_6_out, and_6_out, and_7_out);
  and and_7 (and_7_out, ~b1_2, b2_2);  // AND_Gate
  and and_8 (and_8_out, b1_2, b2_2);
  or or_7 (or_7_out, or_6_out, and_8_out);
  and and_9 (and_9_out, b3_2, b5_2);
  and and_10 (B00_2, and_9_out, or_7_out);
endmodule

module SubCircuito_C (
  input  in_1
);

  Clock clock_1 ();  // open: out
endmodule
